// Logisim project P1.circ as structural Verilog
module OneBitAdder (
  input  A,
  input  B,
  input  C_IN,
  output S,
  output C_OUT
);

  wire and_1_out, and_2_out, xor_1_out;

  xor xor_1 (xor_1_out, A, B);
  xor xor_2 (S, xor_1_out, C_IN);
  and and_1 (and_1_out, C_IN, xor_1_out);
  and and_2 (and_2_out, A, B);
  or or_1 (C_OUT, and_1_out, and_2_out);
endmodule

// 0
module EightBitAdder (
  input  [7:0] A,
  input  [7:0] B,
  input  C_IN,
  output [7:0] S
);

  wire onebitadder_1_c_out, onebitadder_2_c_out, onebitadder_3_c_out, onebitadder_4_c_out,
       onebitadder_5_c_out, onebitadder_6_c_out, onebitadder_7_c_out;

  OneBitAdder onebitadder_1 (.A(A[0]), .B(B[0]), .C_IN(C_IN), .S(S[0]), .C_OUT(onebitadder_1_c_out));
  OneBitAdder onebitadder_2 (.A(A[1]), .B(B[1]), .C_IN(onebitadder_1_c_out), .S(S[1]), .C_OUT(onebitadder_2_c_out));
  OneBitAdder onebitadder_3 (.A(A[2]), .B(B[2]), .C_IN(onebitadder_2_c_out), .S(S[2]), .C_OUT(onebitadder_3_c_out));
  OneBitAdder onebitadder_4 (.A(A[3]), .B(B[3]), .C_IN(onebitadder_3_c_out), .S(S[3]), .C_OUT(onebitadder_4_c_out));
  OneBitAdder onebitadder_5 (.A(A[4]), .B(B[4]), .C_IN(onebitadder_4_c_out), .S(S[4]), .C_OUT(onebitadder_5_c_out));
  OneBitAdder onebitadder_6 (.A(A[5]), .B(B[5]), .C_IN(onebitadder_5_c_out), .S(S[5]), .C_OUT(onebitadder_6_c_out));
  OneBitAdder onebitadder_7 (.A(A[6]), .B(B[6]), .C_IN(onebitadder_6_c_out), .S(S[6]), .C_OUT(onebitadder_7_c_out));
  OneBitAdder onebitadder_8 (.A(A[7]), .B(B[7]), .C_IN(onebitadder_7_c_out), .S(S[7]));  // open: C_OUT
endmodule

module AddSub (
  input  [7:0] A,
  input  ControlAddSub,
  input  [7:0] B,
  output [7:0] RESULT
);

  wire [7:0] xor_1_out;

  xor xor_1 (xor_1_out[0], B[0], ControlAddSub);
  xor xor_2 (xor_1_out[1], B[1], ControlAddSub);
  xor xor_3 (xor_1_out[2], B[2], ControlAddSub);
  xor xor_4 (xor_1_out[3], B[3], ControlAddSub);
  xor xor_5 (xor_1_out[4], B[4], ControlAddSub);
  xor xor_6 (xor_1_out[5], B[5], ControlAddSub);
  xor xor_7 (xor_1_out[6], B[6], ControlAddSub);
  xor xor_8 (xor_1_out[7], B[7], ControlAddSub);
  EightBitAdder eightbitadder_1 (.A(A), .B(xor_1_out), .C_IN(ControlAddSub), .S(RESULT));
endmodule

module ALU (
  input  [3:0] OP,
  input  [7:0] X_OUT,
  input  [7:0] Y,
  output [7:0] X_IN
);

  wire decoder_1_out0, decoder_1_out1, decoder_1_out2, decoder_1_out3, decoder_1_out4, decoder_1_out5,
       decoder_1_out6, decoder_1_out7, or_1_out, or_2_out;
  wire [7:0] addsub_1_result, and_1_out, lshrsh_1_result, not_1_out, or_3_out, xor_1_out;

  Decoder #(.select(3)) decoder_1 (
    .out0(decoder_1_out0), .out1(decoder_1_out1), .out2(decoder_1_out2), .out3(decoder_1_out3),
    .out4(decoder_1_out4), .out5(decoder_1_out5), .out6(decoder_1_out6), .out7(decoder_1_out7),
    .sel(OP[2:0]), .en(OP[3]));
  or or_1 (or_1_out, decoder_1_out1, decoder_1_out0);
  or or_2 (or_2_out, decoder_1_out3, decoder_1_out2);
  AddSub addsub_1 (.A(X_OUT), .ControlAddSub(decoder_1_out1), .B(Y), .RESULT(addsub_1_result));
  LSHRSH lshrsh_1 (.LeftOrRight(decoder_1_out3), .A(X_OUT), .RESULT(lshrsh_1_result));
  assign xor_1_out = X_OUT ^ Y;  // XOR_Gate xor_1, 8 bits wide
  assign not_1_out = ~X_OUT;  // NOT_Gate not_1, 8 bits wide
  assign and_1_out = X_OUT & Y;  // AND_Gate and_1, 8 bits wide
  assign or_3_out = X_OUT | Y;  // OR_Gate or_3, 8 bits wide
  assign X_IN = or_1_out ? addsub_1_result : 8'bz;  // Controlled_Buffer controlled_buffer_1
  assign X_IN = or_2_out ? lshrsh_1_result : 8'bz;  // Controlled_Buffer controlled_buffer_2
  assign X_IN = decoder_1_out4 ? xor_1_out : 8'bz;  // Controlled_Buffer controlled_buffer_3
  assign X_IN = decoder_1_out5 ? not_1_out : 8'bz;  // Controlled_Buffer controlled_buffer_4
  assign X_IN = decoder_1_out6 ? and_1_out : 8'bz;  // Controlled_Buffer controlled_buffer_5
  assign X_IN = decoder_1_out7 ? or_3_out : 8'bz;  // Controlled_Buffer controlled_buffer_6

  // Notes on the sheet:
  //   000 - Add
  //   001 - Sub
  //   011 - Lsh
  //   010 - Rsh
  //   100 - XOR
  //   101 - NOT
  //   110 - AND
  //   111 - OR
endmodule

module LSHRSH (
  input  LeftOrRight,
  input  [7:0] A,
  output [7:0] RESULT
);

  Multiplexer #(.width(8)) multiplexer_1 (.in0({1'b0, A[7:1]}), .in1({A[6:0], 1'b0}), .out(RESULT), .sel(LeftOrRight));
endmodule

module TheStack (
  input  [3:0] OP,
  input  CLK,
  input  RESET,
  input  [7:0] X_IN,
  output [7:0] Y_OUT,
  output [7:0] X_OUT
);

  wire and_1_out, and_2_out, and_3_out, and_4_out, and_5_out, decoder_1_out0, decoder_1_out1, decoder_1_out2,
       decoder_1_out3, decoder_1_out4, decoder_1_out5, decoder_1_out6, decoder_1_out7, not_1_out, not_2_out,
       not_3_out, not_4_out, or_1_out, or_2_out, or_3_out, or_4_out, or_5_out, or_6_out, or_7_out, or_8_out,
       or_9_out;
  wire [7:0] controlled_buffer_1_out, controlled_buffer_3_out, multiplexer_1_out, multiplexer_2_out,
       multiplexer_3_out, multiplexer_4_out, T_q, X0_q, Z_q;

  assign controlled_buffer_1_out = or_1_out ? X_IN : 8'bz;  // Controlled_Buffer controlled_buffer_1
  and and_1 (and_1_out, OP[3], or_4_out);
  and and_2 (and_2_out, OP[3], not_3_out);
  and and_3 (and_3_out, OP[3], not_1_out);
  Decoder #(.select(3)) decoder_1 (
    .out0(decoder_1_out0), .out1(decoder_1_out1), .out2(decoder_1_out2), .out3(decoder_1_out3),
    .out4(decoder_1_out4), .out5(decoder_1_out5), .out6(decoder_1_out6), .out7(decoder_1_out7), .sel(OP[2:0]));  // open: en
  and and_4 (and_4_out, OP[3], not_2_out);
  and and_5 (and_5_out, OP[3], or_7_out);
  or or_1 (or_1_out, decoder_1_out0, decoder_1_out1, decoder_1_out2);
  or or_2 (or_2_out, decoder_1_out0, decoder_1_out1);
  not not_1 (not_1_out, or_2_out);
  or or_3 (or_3_out, or_2_out, decoder_1_out3);
  not not_2 (not_2_out, or_3_out);
  or or_4 (or_4_out, decoder_1_out1, decoder_1_out2);
  not not_3 (not_3_out, decoder_1_out4);
  or or_5 (or_5_out, decoder_1_out3, or_6_out);
  or or_6 (or_6_out, decoder_1_out4, decoder_1_out5);
  or or_7 (or_7_out, or_6_out, decoder_1_out7);
  or or_8 (or_8_out, decoder_1_out6, decoder_1_out7);
  or or_9 (or_9_out, or_8_out, decoder_1_out3);
  not not_4 (not_4_out, or_9_out);
  Register T (.D(multiplexer_1_out), .en(and_5_out), .clk(CLK), .Q(T_q), .clr(RESET));
  Multiplexer #(.width(8)) multiplexer_1 (
    .in0(X_OUT), .in1(controlled_buffer_3_out), .out(multiplexer_1_out), .sel(or_6_out));
  Register Z (.D(multiplexer_2_out), .en(and_4_out), .clk(CLK), .Q(Z_q), .clr(RESET));
  Multiplexer #(.width(8)) multiplexer_2 (.in0(T_q), .in1(Y_OUT), .out(multiplexer_2_out), .sel(or_6_out));
  Register Y (.D(multiplexer_3_out), .en(and_3_out), .clk(CLK), .Q(Y_OUT), .clr(RESET));
  Multiplexer #(.width(8)) multiplexer_3 (
    .in0(controlled_buffer_3_out), .in1(X_OUT), .out(multiplexer_3_out), .sel(or_5_out));
  Register X (.D(multiplexer_4_out), .en(and_2_out), .clk(CLK), .Q(X_OUT), .clr(RESET));
  Multiplexer #(.width(8)) multiplexer_4 (
    .in0(Y_OUT), .in1(controlled_buffer_1_out), .out(multiplexer_4_out), .sel(not_4_out));
  Register X0 (.D(X_OUT), .en(and_1_out), .clk(CLK), .Q(X0_q), .clr(RESET));
  assign controlled_buffer_1_out = or_8_out ? T_q : 8'bz;  // Controlled_Buffer controlled_buffer_2
  assign controlled_buffer_3_out = and_4_out ? Z_q : 8'bz;  // Controlled_Buffer controlled_buffer_3
  assign controlled_buffer_1_out = decoder_1_out5 ? X0_q : 8'bz;  // Controlled_Buffer controlled_buffer_4

  // Notes on the sheet:
  //   1000 - LOAD
  //   1001 -  ALU_UN
  //   1010 - ALU_BIN
  //   1011 - EXY
  //   1100 - PTS
  //   1101 - RPV
  //   1110 - POP
  //   1111 - RTS
  //   Remove this gate in implementation
  //   LOAD
  //   ALU_UN
  //   ALU_BIN
  //   EXY
  //   PTS
  //   RPV
  //   POP
  //   RTS
endmodule

module RegisterFile (
  input  CLK,
  input  RESET,
  input  [3:0] REGISTER_ID,
  input  WVR,
  input  INDIRECT_OP,
  input  RVR,
  input  [7:0] X_OUT,
  input  [7:0] Y_OUT,
  output [7:0] ADDRESS_OUT,
  output [7:0] X_IN
);

  wire and_1_out, and_2_out, and_3_out, and_4_out, and_5_out, and_6_out, decoder_1_out1, decoder_1_out2,
       decoder_1_out3, decoder_1_out4, decoder_1_out5, decoder_1_out6, decoder_1_out7, decoder_1_out8,
       decoder_1_out9, decoder_1_out10, decoder_1_out11, decoder_1_out12, decoder_1_out13, decoder_1_out14,
       decoder_1_out15, decoder_2_out0, decoder_2_out1, decoder_2_out2, decoder_2_out3, decoder_2_out4,
       decoder_2_out5, decoder_2_out6, decoder_2_out7, decoder_2_out8, decoder_2_out9, decoder_2_out10,
       decoder_2_out11, decoder_2_out12, decoder_2_out13, decoder_2_out14, decoder_2_out15, not_1_out,
       not_2_out, not_3_out, or_1_out, or_2_out, or_3_out, or_4_out, or_5_out;
  wire [7:0] addsub_1_result, multiplexer_1_out, R1_q, R2_q, R3_q, R4_q, R5_q, R6_q, R7_q, R8_q, R9_q, R10_q,
       R11_q, R12_q, R13_q, R14_q, R15_q;

  not not_1 (not_1_out, REGISTER_ID[3]);
  not not_2 (not_2_out, REGISTER_ID[2]);
  Multiplexer #(.width(8)) multiplexer_1 (
    .in0(X_OUT), .in1(addsub_1_result), .out(multiplexer_1_out), .sel(INDIRECT_OP));
  not not_3 (not_3_out, REGISTER_ID[1]);
  and and_1 (and_1_out, not_1_out, not_2_out, REGISTER_ID[0]);
  and and_2 (and_2_out, not_1_out, not_2_out, REGISTER_ID[1]);
  and and_3 (and_3_out, not_1_out, REGISTER_ID[2], not_3_out);
  and and_4 (and_4_out, REGISTER_ID[3], REGISTER_ID[2]);
  and and_5 (and_5_out, REGISTER_ID[3], REGISTER_ID[1], REGISTER_ID[0]);
  or or_1 (or_1_out, and_4_out, and_5_out);
  or or_2 (or_2_out, and_1_out, and_2_out, and_3_out);
  or or_3 (or_3_out, or_1_out, or_2_out);
  and and_6 (and_6_out, or_3_out, INDIRECT_OP);
  or or_4 (or_4_out, WVR, and_6_out);
  Decoder #(.select(4)) decoder_1 (
    .out1(decoder_1_out1), .out2(decoder_1_out2), .out3(decoder_1_out3), .out4(decoder_1_out4),
    .out5(decoder_1_out5), .out6(decoder_1_out6), .out7(decoder_1_out7), .out8(decoder_1_out8),
    .out9(decoder_1_out9), .out10(decoder_1_out10), .out11(decoder_1_out11), .out12(decoder_1_out12),
    .out13(decoder_1_out13), .out14(decoder_1_out14), .out15(decoder_1_out15), .sel(REGISTER_ID),
    .en(or_4_out));  // open: out0
  or or_5 (or_5_out, RVR, INDIRECT_OP);
  Decoder #(.select(4)) decoder_2 (
    .out0(decoder_2_out0), .out1(decoder_2_out1), .out2(decoder_2_out2), .out3(decoder_2_out3),
    .out4(decoder_2_out4), .out5(decoder_2_out5), .out6(decoder_2_out6), .out7(decoder_2_out7),
    .out8(decoder_2_out8), .out9(decoder_2_out9), .out10(decoder_2_out10), .out11(decoder_2_out11),
    .out12(decoder_2_out12), .out13(decoder_2_out13), .out14(decoder_2_out14), .out15(decoder_2_out15),
    .sel(REGISTER_ID), .en(or_5_out));
  Register R1 (.D(multiplexer_1_out), .en(decoder_1_out1), .clk(CLK), .Q(R1_q), .clr(RESET));
  Register R2 (.D(multiplexer_1_out), .en(decoder_1_out2), .clk(CLK), .Q(R2_q), .clr(RESET));
  Register R3 (.D(multiplexer_1_out), .en(decoder_1_out3), .clk(CLK), .Q(R3_q), .clr(RESET));
  Register R4 (.D(multiplexer_1_out), .en(decoder_1_out4), .clk(CLK), .Q(R4_q), .clr(RESET));
  Register R5 (.D(multiplexer_1_out), .en(decoder_1_out5), .clk(CLK), .Q(R5_q), .clr(RESET));
  Register R6 (.D(multiplexer_1_out), .en(decoder_1_out6), .clk(CLK), .Q(R6_q), .clr(RESET));
  Register R7 (.D(multiplexer_1_out), .en(decoder_1_out7), .clk(CLK), .Q(R7_q), .clr(RESET));
  Register R8 (.D(multiplexer_1_out), .en(decoder_1_out8), .clk(CLK), .Q(R8_q), .clr(RESET));
  Register R9 (.D(multiplexer_1_out), .en(decoder_1_out9), .clk(CLK), .Q(R9_q), .clr(RESET));
  Register R10 (.D(multiplexer_1_out), .en(decoder_1_out10), .clk(CLK), .Q(R10_q), .clr(RESET));
  Register R11 (.D(multiplexer_1_out), .en(decoder_1_out11), .clk(CLK), .Q(R11_q), .clr(RESET));
  Register R12 (.D(multiplexer_1_out), .en(decoder_1_out12), .clk(CLK), .Q(R12_q), .clr(RESET));
  Register R13 (.D(multiplexer_1_out), .en(decoder_1_out13), .clk(CLK), .Q(R13_q), .clr(RESET));
  Register R14 (.D(multiplexer_1_out), .en(decoder_1_out14), .clk(CLK), .Q(R14_q), .clr(RESET));
  Register R15 (.D(multiplexer_1_out), .en(decoder_1_out15), .clk(CLK), .Q(R15_q), .clr(RESET));
  assign ADDRESS_OUT = decoder_2_out1 ? R1_q : 8'bz;  // Controlled_Buffer controlled_buffer_1
  assign ADDRESS_OUT = decoder_2_out2 ? R2_q : 8'bz;  // Controlled_Buffer controlled_buffer_2
  assign ADDRESS_OUT = decoder_2_out3 ? R3_q : 8'bz;  // Controlled_Buffer controlled_buffer_3
  assign ADDRESS_OUT = decoder_2_out4 ? R4_q : 8'bz;  // Controlled_Buffer controlled_buffer_4
  assign ADDRESS_OUT = decoder_2_out5 ? R5_q : 8'bz;  // Controlled_Buffer controlled_buffer_5
  assign ADDRESS_OUT = decoder_2_out6 ? R6_q : 8'bz;  // Controlled_Buffer controlled_buffer_6
  assign ADDRESS_OUT = decoder_2_out7 ? R7_q : 8'bz;  // Controlled_Buffer controlled_buffer_7
  assign ADDRESS_OUT = decoder_2_out8 ? R8_q : 8'bz;  // Controlled_Buffer controlled_buffer_8
  assign ADDRESS_OUT = decoder_2_out9 ? R9_q : 8'bz;  // Controlled_Buffer controlled_buffer_9
  assign ADDRESS_OUT = decoder_2_out10 ? R10_q : 8'bz;  // Controlled_Buffer controlled_buffer_10
  assign ADDRESS_OUT = decoder_2_out11 ? R11_q : 8'bz;  // Controlled_Buffer controlled_buffer_11
  assign ADDRESS_OUT = decoder_2_out12 ? R12_q : 8'bz;  // Controlled_Buffer controlled_buffer_12
  assign ADDRESS_OUT = decoder_2_out13 ? R13_q : 8'bz;  // Controlled_Buffer controlled_buffer_13
  assign ADDRESS_OUT = decoder_2_out14 ? R14_q : 8'bz;  // Controlled_Buffer controlled_buffer_14
  assign ADDRESS_OUT = decoder_2_out15 ? R15_q : 8'bz;  // Controlled_Buffer controlled_buffer_15
  assign ADDRESS_OUT = decoder_2_out0 ? Y_OUT : 8'bz;  // Controlled_Buffer controlled_buffer_16
  AddSub addsub_1 (.A(ADDRESS_OUT), .ControlAddSub(or_2_out), .B(8'h1), .RESULT(addsub_1_result));

  assign X_IN = ADDRESS_OUT;
endmodule

module CPU (
  input  CLK,
  input  RESET
);

  wire [7:0] registerfile_1_x_in, thestack_1_x_out, thestack_1_y_out;

  TheStack thestack_1 (
    .CLK(CLK), .RESET(RESET), .X_IN(registerfile_1_x_in), .Y_OUT(thestack_1_y_out), .X_OUT(thestack_1_x_out));  // open: OP
  RegisterFile registerfile_1 (
    .CLK(CLK), .RESET(RESET), .X_OUT(thestack_1_x_out), .Y_OUT(thestack_1_y_out), .X_IN(registerfile_1_x_in));  // open: REGISTER_ID, WVR, INDIRECT_OP, RVR, ADDRESS_OUT
  // ALU alu_1: pin names not known; wires that end beside it: thestack_1_x_out, thestack_1_y_out, registerfile_1_x_in
endmodule
